# Fritzing sketch circuit (saved by Fritzing 0.9.3b)
breadboards: 1

parts:
  MCU1 = Raspberry Pi Zero
  IC1 = MCP3008 8-channel 10-bit ADC [part_number=MCP3008]
  R1 = Temperature Sensor (Thermistor) [thermistor_type=NTC package=THT]
  R2 = Resistor [tolerance=±5% resistance=10k package=THT]
  D1 = Rectifier Diode [part_number=1N4001 package="300 mil [THT]"]
  S1 = Round Pushbutton
  S2 = Round Pushbutton
  LED2 = smd LED [color="Blue (505nm)" package="0603 [SMD]"]
  U1 = RELAY-SOLIDSTATE [package=relay-s108t02]
  R3 = Resistor [tolerance=±5% resistance=20k package=THT]
  Q1 = TRANSISTOR_NPN [package=to-92]
  R5 = Resistor [tolerance=±5% resistance=10k package=THT]
  R6 = Resistor [tolerance=±5% resistance=10k package=THT]

nets:
  N1: MCU1.pin_1, MCU1.pin_17, IC1.no_name_yet#15, R1.pin_1
  N2: MCU1.pin_6, MCU1.pin_9, MCU1.pin_20, MCU1.pin_24, MCU1.pin_25, MCU1.pin_30, MCU1.pin_34, IC1.no_name_yet#9, IC1.no_name_yet#10, IC1.no_name_yet#14, R2.Pin_1, S1.leg0, S2.leg1, LED2.cathode, U1.-, Q1.E, Q1.B, Q1.C, R5.Pin_0, R5.Pin_1, R6.Pin_0
  N3: MCU1.pin_11, R6.Pin_1
  N4: MCU1.pin_13, S1.leg1
  N5: MCU1.pin_15, S2.leg0
  N6: MCU1.pin_19, IC1.no_name_yet#11
  N7: MCU1.pin_21, IC1.no_name_yet#12
  N8: MCU1.pin_23, IC1.no_name_yet#13
  N9: MCU1.pin_37, R3.Pin_1
  N10: IC1.no_name_yet#1, R1.pin_0, R2.Pin_0
  N11: D1.anode, U1.+
  N12: LED2.anode, R3.Pin_0

notes:
  Power Adapter
  In: 120V, 0.35A
  Out: 5V, 2A
  5 NeoPixels
  Thermistor
  120V, 0.15A Drink Heater
  Solid State Relay
  In: 5V, 20mA
  Out: 240V, 2A
  MCP3008
  8-Channel
  10-bit ADC
  Raspberry Pi Zero W
  NPN
  2N2222
  "Ready"
  LED
